# Fritzing sketch shift_register_x2_led_x10 (saved by Fritzing 0.9.3b)
breadboards: 1

parts:
  パーツ1 = Arduino Uno (Rev3)
  U1 = 74HC595 [package="DIP16 [THT]"]
  U2 = 74HC595 [package="DIP16 [THT]"]
  LED1 = LED - 5mm [color="Red (633nm)" package="5 mm [THT]"]
  LED2 = LED - 5mm [color="Red (633nm)" package="5 mm [THT]"]
  LED5 = LED - 5mm [color="Red (633nm)" package="5 mm [THT]"]
  LED6 = LED - 5mm [color="Red (633nm)" package="5 mm [THT]"]
  LED7 = LED - 5mm [color="Red (633nm)" package="5 mm [THT]"]
  LED8 = LED - 5mm [color="Red (633nm)" package="5 mm [THT]"]
  LED9 = LED - 5mm [color="Red (633nm)" package="5 mm [THT]"]
  LED10 = LED - 5mm [color="Red (633nm)" package="5 mm [THT]"]
  R1 = Resistor [tolerance=±5% resistance=150 package=THT]
  R2 = Resistor [tolerance=±5% resistance=150 package=THT]
  R3 = Resistor [tolerance=±5% resistance=150 package=THT]
  R4 = Resistor [tolerance=±5% resistance=150 package=THT]
  R5 = Resistor [tolerance=±5% resistance=150 package=THT]
  R6 = Resistor [tolerance=±5% resistance=150 package=THT]
  R7 = Resistor [tolerance=±5% resistance=150 package=THT]
  R8 = Resistor [tolerance=±5% resistance=150 package=THT]
  R9 = Resistor [tolerance=±5% resistance=150 package=THT]
  R10 = Resistor [tolerance=±5% resistance=150 package=THT]
  LED4 = LED - 5mm [color="Red (633nm)" package="5 mm [THT]"]
  LED3 = LED - 5mm [color="Red (633nm)" package="5 mm [THT]"]

nets:
  N1: パーツ1.D2, U1.DS
  N2: パーツ1.D3_PWM, U1.SH_CP, U2.SH_CP
  N3: パーツ1.D4, U1.ST_CP, U2.ST_CP
  VCC: パーツ1.5V, U1.MR, U1.VCC, U2.MR, U2.VCC
  GND: パーツ1.GND, U1.GND, U1.OE, U2.GND, U2.OE, LED1.cathode, LED2.cathode, LED5.cathode, LED6.cathode, LED7.cathode, LED8.cathode, LED9.cathode, LED10.cathode, LED4.cathode, LED3.cathode
  N4: U1.Q1, R2.Pin_0
  N5: U1.Q2, R3.Pin_0
  N6: U1.Q3, R4.Pin_0
  N7: U1.Q4, R5.Pin_0
  N8: U1.Q5, R6.Pin_0
  N9: U1.Q6, R7.Pin_0
  N10: U1.Q7, R8.Pin_0
  N11: U1.Q7', U2.DS
  N12: U1.Q0, R1.Pin_0
  N13: U2.Q1, R10.Pin_0
  N14: U2.Q0, R9.Pin_0
  N15: LED1.anode, R10.Pin_1
  N16: LED2.anode, R1.Pin_1
  N17: LED5.anode, R7.Pin_1
  N18: LED6.anode, R5.Pin_1
  N19: LED7.anode, R2.Pin_1
  N20: LED8.anode, R3.Pin_1
  N21: LED9.anode, R4.Pin_1
  N22: LED10.anode, R6.Pin_1
  N23: R8.Pin_1, LED4.anode
  N24: R9.Pin_1, LED3.anode
